// Digital circuit contmod5.dig as structural Verilog
module contmod5 (
  input  in_2,
  input  in_3,
  input  in_4,
  output [2:0] out_1
);

  contmod5 #(.applicationType("GHDL"), .CodeFile("D:\\github\\uffs-arquivos\\SEM3\\sistemas-digitais\\FSM\\contmod5\\contmod5.vhd")) u_contmod5 (
    .S(in_2), .CLK(in_4), .reset(in_3), .cont(out_1));
endmodule
