// Digital circuit busArbiter.dig as structural Verilog
module busArbiter (
  input  in_1,
  input  in_2,
  input  in_3,
  input  in_4,
  input  in_5,
  input  clk,
  output out_6,
  output out_7,
  output out_8,
  output out_9
);

  busArbiter #(.applicationType("GHDL"), .CodeFile("D:\\github\\uffs-arquivos\\SEM3\\sistemas-digitais\\T02\\busArbiter.vhd")) u_busArbiter (
    .clk(clk), .reset(in_1), .req0(in_2), .req1(in_3), .req2(in_4), .req3(in_5), .aut0(out_6), .aut1(out_7),
    .aut2(out_8), .aut3(out_9));
endmodule
