// Digital circuit busArbiterCompleto.dig as structural Verilog
module busArbiterCompleto (
  input  [3:0] in_2,
  input  [9:0] in_3,
  input  in_4,
  output [9:0] out_1
);

  wire dipswitch_1_out, dipswitch_2_out, dipswitch_3_out, dipswitch_4_out, dipswitch_5_out,
       u_busArbiter_2_aut0, u_busArbiter_2_aut1, u_busArbiter_2_aut2, u_busArbiter_2_aut3;

  DipSwitch dipswitch_1 (.out(dipswitch_1_out));
  DipSwitch dipswitch_2 (.out(dipswitch_2_out));
  DipSwitch dipswitch_3 (.out(dipswitch_3_out));
  DipSwitch dipswitch_4 (.out(dipswitch_4_out));
  DipSwitch dipswitch_5 (.out(dipswitch_5_out));
  busArbiter #(.applicationType("GHDL"), .CodeFile("D:\\github\\uffs-arquivos\\SEM3\\sistemas-digitais\\T02\\codigofpgaArrumado.vhd")) u_busArbiter (
    .KEY(in_2), .sw(in_3), .ledR(out_1));
  busArbiter #(.applicationType("GHDL"), .CodeFile("D:\\github\\uffs-arquivos\\SEM3\\sistemas-digitais\\T02\\busArbiterOriginal.vhd")) u_busArbiter_2 (
    .clk(in_4), .reset(dipswitch_1_out), .req0(dipswitch_2_out), .req1(dipswitch_3_out),
    .req2(dipswitch_4_out), .req3(dipswitch_5_out), .aut0(u_busArbiter_2_aut0), .aut1(u_busArbiter_2_aut1),
    .aut2(u_busArbiter_2_aut2), .aut3(u_busArbiter_2_aut3));
  LED led_1 (.in(u_busArbiter_2_aut0));
  LED led_2 (.in(u_busArbiter_2_aut1));
  LED led_3 (.in(u_busArbiter_2_aut2));
  LED led_4 (.in(u_busArbiter_2_aut3));
endmodule
