// Digital circuit blackjack.dig as structural Verilog
module blackjack (
  input  [9:0] in_1,
  input  [9:0] in_2,
  input  [3:0] in_3,
  input  in_4,
  input  in_6,
  input  in_7,
  input  in_8,
  input  in_9,
  input  in_10,
  input  in_11,
  input  in_12,
  input  in_13,
  input  in_14,
  input  in_15,
  input  in_16,
  input  in_17,
  input  in_18,
  output [6:0] out_5
);

  wire bussplitter_1_d0, bussplitter_1_d1, bussplitter_1_d2, bussplitter_1_d3, bussplitter_1_d4,
       bussplitter_1_d5, bussplitter_1_d6, bussplitter_1_d7, bussplitter_1_d8, bussplitter_1_d9,
       bussplitter_2_d0, bussplitter_2_d1, bussplitter_2_d2, bussplitter_2_d3, bussplitter_2_d4,
       bussplitter_2_d5, bussplitter_2_d6, bussplitter_2_d7, bussplitter_2_d8, bussplitter_2_d9,
       bussplitter_3_d0, bussplitter_3_d1, bussplitter_3_d2, bussplitter_3_d3, bussplitter_3_d4,
       bussplitter_3_d5, bussplitter_3_d6, bussplitter_4_d0, bussplitter_4_d1, bussplitter_4_d2,
       bussplitter_4_d3, bussplitter_4_d4, bussplitter_4_d5, bussplitter_4_d6, bussplitter_5_d0,
       bussplitter_5_d1, bussplitter_5_d2, bussplitter_5_d3, bussplitter_5_d4, bussplitter_5_d5,
       bussplitter_5_d6, bussplitter_6_d0, bussplitter_6_d1, bussplitter_6_d2, bussplitter_6_d3,
       bussplitter_6_d4, bussplitter_6_d5, bussplitter_6_d6;
  wire [6:0] not_1_out, not_2_out, not_3_out, not_4_out, u_blackJack_hex0, u_blackJack_hex1,
       u_blackJack_hex2, u_teste_hex0;
  wire [9:0] u_blackJack_ledg, u_blackJack_ledr;

  blackJack #(.applicationType("GHDL"), .CodeFile("D:\\github\\uffs-arquivos\\SEM3\\sistemas-digitais\\TF\\blackjack.vhd")) u_blackJack (
    .KEY(in_1), .sw(in_2), .CLK(in_4), .card(in_3), .hit(in_6), .stay(in_7), .ledR(u_blackJack_ledr),
    .ledG(u_blackJack_ledg), .hex0(u_blackJack_hex0), .hex1(u_blackJack_hex1), .hex2(u_blackJack_hex2),
    .hex3(out_5));
  BusSplitter #(.Bits(10)) bussplitter_1 (
    .D(u_blackJack_ledr), .OE(in_8), .D0(bussplitter_1_d0), .D1(bussplitter_1_d1), .D2(bussplitter_1_d2),
    .D3(bussplitter_1_d3), .D4(bussplitter_1_d4), .D5(bussplitter_1_d5), .D6(bussplitter_1_d6),
    .D7(bussplitter_1_d7), .D8(bussplitter_1_d8), .D9(bussplitter_1_d9));
  LED led_1 (.in(bussplitter_1_d9));
  LED led_2 (.in(bussplitter_1_d8));
  LED led_3 (.in(bussplitter_1_d7));
  LED led_4 (.in(bussplitter_1_d6));
  LED led_5 (.in(bussplitter_1_d5));
  LED led_6 (.in(bussplitter_1_d4));
  LED led_7 (.in(bussplitter_1_d3));
  LED led_8 (.in(bussplitter_1_d2));
  LED led_9 (.in(bussplitter_1_d1));
  LED led_10 (.in(bussplitter_1_d0));
  assign not_1_out = ~u_blackJack_hex2;  // Not not_1, 7 bits wide
  LED led_11 (.in(bussplitter_2_d9));
  LED led_12 (.in(bussplitter_2_d8));
  LED led_13 (.in(bussplitter_2_d7));
  LED led_14 (.in(bussplitter_2_d6));
  LED led_15 (.in(bussplitter_2_d5));
  LED led_16 (.in(bussplitter_2_d4));
  LED led_17 (.in(bussplitter_2_d3));
  LED led_18 (.in(bussplitter_2_d2));
  LED led_19 (.in(bussplitter_2_d1));
  BusSplitter #(.Bits(10)) bussplitter_2 (
    .D(u_blackJack_ledg), .OE(in_9), .D0(bussplitter_2_d0), .D1(bussplitter_2_d1), .D2(bussplitter_2_d2),
    .D3(bussplitter_2_d3), .D4(bussplitter_2_d4), .D5(bussplitter_2_d5), .D6(bussplitter_2_d6),
    .D7(bussplitter_2_d7), .D8(bussplitter_2_d8), .D9(bussplitter_2_d9));
  LED led_20 (.in(bussplitter_2_d0));
  BusSplitter #(.Bits(7)) bussplitter_3 (
    .D(not_1_out), .OE(in_15), .D0(bussplitter_3_d0), .D1(bussplitter_3_d1), .D2(bussplitter_3_d2),
    .D3(bussplitter_3_d3), .D4(bussplitter_3_d4), .D5(bussplitter_3_d5), .D6(bussplitter_3_d6));
  Seven_Seg seven_seg_1 (
    .a(bussplitter_3_d0), .b(bussplitter_3_d1), .c(bussplitter_3_d2), .d(bussplitter_3_d3),
    .e(bussplitter_3_d4), .f(bussplitter_3_d5), .g(bussplitter_3_d6), .dp(in_16));
  assign not_2_out = ~u_blackJack_hex0;  // Not not_2, 7 bits wide
  assign not_3_out = ~u_blackJack_hex1;  // Not not_3, 7 bits wide
  BusSplitter #(.Bits(7)) bussplitter_4 (
    .D(not_2_out), .OE(in_13), .D0(bussplitter_4_d0), .D1(bussplitter_4_d1), .D2(bussplitter_4_d2),
    .D3(bussplitter_4_d3), .D4(bussplitter_4_d4), .D5(bussplitter_4_d5), .D6(bussplitter_4_d6));
  BusSplitter #(.Bits(7)) bussplitter_5 (
    .D(not_3_out), .OE(in_17), .D0(bussplitter_5_d0), .D1(bussplitter_5_d1), .D2(bussplitter_5_d2),
    .D3(bussplitter_5_d3), .D4(bussplitter_5_d4), .D5(bussplitter_5_d5), .D6(bussplitter_5_d6));
  Seven_Seg seven_seg_2 (
    .a(bussplitter_4_d0), .b(bussplitter_4_d1), .c(bussplitter_4_d2), .d(bussplitter_4_d3),
    .e(bussplitter_4_d4), .f(bussplitter_4_d5), .g(bussplitter_4_d6), .dp(in_14));
  Seven_Seg seven_seg_3 (
    .a(bussplitter_5_d0), .b(bussplitter_5_d1), .c(bussplitter_5_d2), .d(bussplitter_5_d3),
    .e(bussplitter_5_d4), .f(bussplitter_5_d5), .g(bussplitter_5_d6), .dp(in_18));
  teste #(.applicationType("GHDL"), .CodeFile("C:\\Users\\aluno\\Documents\\GitHub\\uffs-arquivos\\SEM3\\sistemas-digitais\\TF\\testesDisplay.vhd")) u_teste (
    .clk(in_10), .hex0(u_teste_hex0));
  assign not_4_out = ~u_teste_hex0;  // Not not_4, 7 bits wide
  BusSplitter #(.Bits(7)) bussplitter_6 (
    .D(not_4_out), .OE(in_11), .D0(bussplitter_6_d0), .D1(bussplitter_6_d1), .D2(bussplitter_6_d2),
    .D3(bussplitter_6_d3), .D4(bussplitter_6_d4), .D5(bussplitter_6_d5), .D6(bussplitter_6_d6));
  Seven_Seg seven_seg_4 (
    .a(bussplitter_6_d0), .b(bussplitter_6_d1), .c(bussplitter_6_d2), .d(bussplitter_6_d3),
    .e(bussplitter_6_d4), .f(bussplitter_6_d5), .g(bussplitter_6_d6), .dp(in_12));

  // Notes on the sheet:
  //   in_1: default 1023
  //   in_3: default 3
  //   in_8: default 1
  //   in_9: default 1
  //   in_11: default 1
  //   in_12: default 1
  //   in_13: default 1
  //   in_14: default 1
  //   in_15: default 1
  //   in_16: default 1
  //   in_17: default 1
  //   in_18: default 1
  //   valor da carta
  //   atual
  //   VALOR DA CARTA
  //   NADA
  //   depois: pontuação
endmodule
