// Digital circuit contDec.dig as structural Verilog
module contDec (
  input  in_1,
  input  in_2,
  input  CLK,
  output out_3,
  output [3:0] out_4
);

  counter_dec #(.applicationType("GHDL"), .CodeFile("D:\\github\\uffs-arquivos\\SEM3\\sistemas-digitais\\vhdl\\contDec\\contDec.vhd")) u_counter_dec (
    .CE(in_1), .CLK(CLK), .RST(in_2), .OV(out_3), .COUNT(out_4));
endmodule
