// Digital circuit dec3to8.dig as structural Verilog
module dec3to8 (
  input  [2:0] in_1,
  output [7:0] out_2
);

  decoder_3to8 #(.applicationType("GHDL"), .CodeFile("/home/aluno/Documentos/GitHub/uffs-arquivos-SD/vhdl/dec3to8/decoder_3to8.vhd")) u_decoder_3to8 (
    .A(in_1), .Y(out_2));
endmodule
