// Digital circuit conv_decTo7Seg.dig as structural Verilog
module conv_decTo7Seg (
  input  [7:0] in_1
);

  wire u_decoder_decTo7Seg_o0, u_decoder_decTo7Seg_o1, u_decoder_decTo7Seg_o2, u_decoder_decTo7Seg_o3,
       u_decoder_decTo7Seg_o4, u_decoder_decTo7Seg_o5, u_decoder_decTo7Seg_o6, u_decoder_decTo7Seg_o7;

  decoder_decTo7Seg #(.applicationType("GHDL"), .CodeFile("D:\\github\\uffs-arquivos\\SEM3\\sistemas-digitais\\vhdl\\decTo7Seg\\decTo7Seg.vhd")) u_decoder_decTo7Seg (
    .I(in_1), .O0(u_decoder_decTo7Seg_o0), .O1(u_decoder_decTo7Seg_o1), .O2(u_decoder_decTo7Seg_o2),
    .O3(u_decoder_decTo7Seg_o3), .O4(u_decoder_decTo7Seg_o4), .O5(u_decoder_decTo7Seg_o5),
    .O6(u_decoder_decTo7Seg_o6), .O7(u_decoder_decTo7Seg_o7));
  Seven_Seg seven_seg_1 (
    .a(u_decoder_decTo7Seg_o0), .b(u_decoder_decTo7Seg_o1), .c(u_decoder_decTo7Seg_o2),
    .d(u_decoder_decTo7Seg_o3), .e(u_decoder_decTo7Seg_o4), .f(u_decoder_decTo7Seg_o5),
    .g(u_decoder_decTo7Seg_o6), .dp(u_decoder_decTo7Seg_o7));
endmodule
