// Digital circuit dec_2to4en.dig as structural Verilog
module dec_2to4en (
  input  in_1,
  input  [1:0] in_2,
  output [3:0] out_3
);

  decoder_2to4en #(.applicationType("GHDL"), .CodeFile("/home/aluno/Documentos/GitHub/uffs-arquivos/SEM3/sistemas-digitais/vhdl/dec_2to4en/dec_2to4en.vhd")) u_decoder_2to4en (
    .EN(in_1), .A(in_2), .Y_L(out_3));
endmodule
