// Digital circuit mux4x1.dig as structural Verilog
module mux4x1 (
  input  [3:0] in_1,
  input  [1:0] in_2,
  output out_3
);

  mux #(.applicationType("GHDL"), .CodeFile("D:\\github\\uffs-arquivos\\SEM3\\sistemas-digitais\\vhdl\\mux4x1\\mux4x1.vhd")) u_mux (
    .I(in_1), .SEL(in_2), .Y(out_3));
endmodule
