// Digital circuit somador.dig as structural Verilog
module somador (
  input  in_5,
  input  in_6,
  input  in_7,
  input  in_8,
  input  in_9,
  input  in_10,
  input  in_11,
  output out_1,
  output out_2,
  output out_3,
  output out_4
);

  adder_3b #(.applicationType("GHDL"), .CodeFile("D:\\github\\uffs-arquivos-SD\\vhdl\\somador\\somador.vhd")) u_adder_3b (
    .A1(in_7), .A2(in_6), .A3(in_5), .B1(in_10), .B2(in_9), .B3(in_8), .Ci1(in_11), .S1(out_3), .S2(out_2),
    .S3(out_1), .Co(out_4));
endmodule
