// Digital circuit teste_incrementador.dig as structural Verilog
module teste_incrementador (
  input  [31:0] in_1,
  output [31:0] out_2
);

  incrementador #(.applicationType("GHDL"), .CodeFile("D:\\github\\uffs-arquivos\\SEM3\\sistemas-digitais\\vhdl\\testes\\incrementador.vhd")) u_incrementador (
    .data_in(in_1), .data_out(out_2));
endmodule
