// Digital circuit testes.dig as structural Verilog
module testes (
  input  in_1,
  input  in_2,
  input  in_3,
  input  in_4,
  input  in_5,
  input  in_6,
  output out_7
);

  mux4x2 #(.applicationType("GHDL")) u_mux4x2 (
    .D0(in_1), .D1(in_3), .D2(in_2), .D3(in_4), .s0(in_6), .s1(in_5), .y(out_7));
  verify_button #(.applicationType("GHDL")) u_verify_button ();  // open: B0, B1, B2, B3, Y
endmodule

/* Code of mux4x2:
library IEEE;
use IEEE.std_logic_1164.all;
use IEEE.numeric_std.all;

entity mux4x2 is 
port (

    	D0, D1, D2, D3 : in std_logic; 
    	s0, s1: in std_logic; 
    	y: out std_logic

); 
end mux4x2; 

architecture behav_mux4x2 of mux4x2 is

    	signal sel : std_logic_vector(1 downto 0) := "00"; 

begin
    	-- concatenação de s1 e s0 para o logic vector 
	sel <= s1 & s0; 
    	
	-- else é obrigatório  
	y <= 	d0 when sel = "00" else 
		d1 when sel = "01" else 
		d2 when sel = "10" else 
		d3; 	
    
end architecture behav_mux4x2;
*/

/* Code of verify_button:
-- sistema que recebe quatro botões e responde se mais de um 
-- for pressionado

library IEEE; 
use IEEE.std_logic_1164.all; 
use IEEE.numeric_std.all;
 

entity verify_button is 
port (
	
	B0, B1, B2, B3: in std_logic; 
	Y: out std_logic
	
);  
end verify_button;

architecture behav_verify_button of verify_button is 
	signal sel : std logic_vector(3 downto 0) := "0000";
begin 
	sel <= b0 & b1 & b2 & b3; 
	with sel select 
		Y <= '0' when "0001" | "0010" | "0100" | "1000", 
		     '1' when others;  	

end architecture behav_verify_button;
*/
