// Digital circuit cicuit.dig as structural Verilog
module cicuit (
  input  in_1
);

  wire not_1_out, not_2_out, not_3_out, u_CONTROLL_alu_in_src, u_CONTROLL_branch, u_CONTROLL_mem_read,
       u_CONTROLL_mem_to_reg, u_CONTROLL_mem_write, u_CONTROLL_reg_write, u_ULA_z;
  wire [2:0] u_CONTROLL_alu_op;
  wire [3:0] add_1_s, add_2_s, multiplexer_1_out, register_1_q, u_IMMGEN_out_imm4, u_INST_DECODER_op_code,
       u_INST_DECODER_out_imm4, u_INST_DECODER_out_rd, u_INST_DECODER_out_rs1, u_INST_DECODER_out_rs2;
  wire [7:0] multiplexer_2_out, u_IMMGEN_out_imm8, u_INST_DECODER_out_imm8;
  wire [15:0] Data_Ram_d, Instruction_Ram_d, multiplexer_3_out, registerfile_1_da, registerfile_1_db, u_ULA_s;

  Register #(.Bits(4)) register_1 (.D(multiplexer_1_out), .C(in_1), .en(1'b1), .Q(register_1_q));
  // Probe on register_1_q
  Multiplexer #(.Bits(4)) multiplexer_1 (
    .sel(u_CONTROLL_branch), .in_0(add_1_s), .in_1(add_2_s), .out(multiplexer_1_out));
  not not_1 (not_1_out, in_1);
  RAMDualPort #(.AddrBits(4), .Bits(16)) Instruction_Ram (
    .A(register_1_q), .Din({16{1'b0}}), .str(1'b0), .C(not_1_out), .ld(1'b1), .D(Instruction_Ram_d));
  Add #(.Bits(4)) add_1 (.a(register_1_q), .b(4'b0001), .c_i(1'b0), .s(add_1_s));  // open: c_o
  // Probe on Instruction_Ram_d
  INST_DECODER #(.applicationType("GHDL"), .CodeFile("D:\\github\\uffs-arquivos\\SEM4\\org\\proc18bits\\instruction_decoder.vhd")) u_INST_DECODER (
    .inst(Instruction_Ram_d), .op_code(u_INST_DECODER_op_code), .out_rd(u_INST_DECODER_out_rd),
    .out_rs1(u_INST_DECODER_out_rs1), .out_rs2(u_INST_DECODER_out_rs2), .out_imm4(u_INST_DECODER_out_imm4),
    .out_imm8(u_INST_DECODER_out_imm8));
  CONTROLL #(.applicationType("GHDL"), .CodeFile("D:\\github\\uffs-arquivos\\SEM4\\org\\proc18bits\\controll.vhd")) u_CONTROLL (
    .inst(u_INST_DECODER_op_code), .zero(u_ULA_z), .branch(u_CONTROLL_branch),
    .mem_write(u_CONTROLL_mem_write), .mem_read(u_CONTROLL_mem_read), .mem_to_reg(u_CONTROLL_mem_to_reg),
    .alu_op(u_CONTROLL_alu_op), .alu_in_src(u_CONTROLL_alu_in_src), .reg_write(u_CONTROLL_reg_write));
  not not_2 (not_2_out, in_1);
  RegisterFile #(.AddrBits(4), .Bits(16)) registerfile_1 (
    .Din(multiplexer_3_out), .we(u_CONTROLL_reg_write), .Rw(u_INST_DECODER_out_rd), .C(not_2_out),
    .Ra(u_INST_DECODER_out_rs1), .Rb(u_INST_DECODER_out_rs2), .Da(registerfile_1_da), .Db(registerfile_1_db));
  IMMGEN #(.applicationType("GHDL"), .CodeFile("D:\\github\\uffs-arquivos\\SEM4\\org\\proc18bits\\imm_gen.vhd")) u_IMMGEN (
    .imm4(u_INST_DECODER_out_imm4), .imm8(u_INST_DECODER_out_imm8), .out_imm4(u_IMMGEN_out_imm4),
    .out_imm8(u_IMMGEN_out_imm8));
  Add #(.Bits(4)) add_2 (.a(register_1_q), .b(u_IMMGEN_out_imm4), .c_i(1'b0), .s(add_2_s));  // open: c_o
  Multiplexer multiplexer_2 (
    .sel(u_CONTROLL_alu_in_src), .in_0(registerfile_1_db[0]), .in_1(u_IMMGEN_out_imm8[0]),
    .out(multiplexer_2_out[0]));
  ULA #(.applicationType("GHDL"), .CodeFile("D:\\github\\uffs-arquivos\\SEM4\\org\\proc18bits\\ula.vhd")) u_ULA (
    .op(u_CONTROLL_alu_op), .a(registerfile_1_da[7:0]), .b(multiplexer_2_out), .z(u_ULA_z), .s(u_ULA_s[7:0]));
  not not_3 (not_3_out, in_1);
  RAMDualPort Data_Ram (
    .A(u_ULA_s[1:0]), .Din(registerfile_1_da[0]), .str(u_CONTROLL_mem_write), .C(not_3_out),
    .ld(u_CONTROLL_mem_read), .D(Data_Ram_d[0]));
  Multiplexer #(.Bits(16)) multiplexer_3 (
    .sel(u_CONTROLL_mem_to_reg), .in_0(Data_Ram_d), .in_1(u_ULA_s), .out(multiplexer_3_out));
  // Pins of 1 and 8 and 16 bits meet at registerfile_1_da
  // Pins of 1 and 16 bits meet at registerfile_1_db
  // Pins of 1 and 8 bits meet at u_IMMGEN_out_imm8
  // Pins of 2 and 8 and 16 bits meet at u_ULA_s
  // Pins of 1 and 16 bits meet at Data_Ram_d
  // Pins of 1 and 8 bits meet at multiplexer_2_out
endmodule
