// Digital circuit testes.dig as structural Verilog
module testes (
  input  in_1,
  input  [7:0] in_6,
  input  [7:0] in_7,
  input  [2:0] in_8,
  input  [11:0] dado_a_ser_armazenado,
  input  \_1___dado_é_armazenado ,
  input  [4:0] seleciona_registrador,
  input  in_14,
  input  [4:0] in_15,
  input  [4:0] in_16,
  input  [4:0] \endereço_onde_pegar___armazenar ,
  input  [11:0] dado_a_ser_armazenado_2,
  input  _1___dado_armazenado_no_clock,
  input  in_23,
  input  in_24,
  input  in_25,
  input  in_26,
  input  in_27,
  output [2:0] out_2,
  output [2:0] out_3,
  output [2:0] out_4,
  output [2:0] out_5,
  output [7:0] out_9,
  output [7:0] out_10,
  output [11:0] out_17,
  output [11:0] out_18,
  output [11:0] out_19,
  output [2:0] out_28,
  output [2:0] out_29,
  output [2:0] out_30,
  output [2:0] out_31,
  output [7:0] out_32
);

  wire u_INST_MEM_CONTROLLER_id, u_INST_MEM_CONTROLLER_str;
  wire [4:0] u_INST_MEM_CONTROLLER_instruction_addrs;
  wire [11:0] ramdualport_1_d, u_INST_MEM_CONTROLLER_din, u_INSTRUCTION_MEMORY_instruction;

  ULA #(.applicationType("GHDL"), .CodeFile("D:\\github\\uffs-arquivos\\SEM4\\org\\processador8bits\\ula.vhd")) u_ULA (
    .a(in_6), .b(in_7), .op(in_8), .s(out_9));
  INSTRUCTION_MEMORY #(.applicationType("GHDL"), .CodeFile("D:\\github\\uffs-arquivos\\SEM4\\org\\processador8bits\\instruction_memory.vhd")) u_INSTRUCTION_MEMORY (
    .clk(in_1), .start(in_25), .instruction(u_INSTRUCTION_MEMORY_instruction));  // open: valid_clk
  RegisterFile #(.AddrBits(5), .Bits(12)) BANCO (
    .Din(dado_a_ser_armazenado), .we(\_1___dado_é_armazenado ), .Rw(seleciona_registrador), .C(in_14),
    .Ra(in_15), .Rb(in_16), .Da(out_17), .Db(out_18));
  INST_MEM_CONTROLLER #(.applicationType("GHDL"), .CodeFile("D:\\github\\uffs-arquivos\\SEM4\\org\\processador8bits\\inst_mem_controller.vhd")) u_INST_MEM_CONTROLLER (
    .clk(in_26), .start(in_27), .instruction_addrs(u_INST_MEM_CONTROLLER_instruction_addrs),
    .din(u_INST_MEM_CONTROLLER_din), .str(u_INST_MEM_CONTROLLER_str), .id(u_INST_MEM_CONTROLLER_id));  // open: valid_clk
  INST_DECODER #(.applicationType("GHDL"), .CodeFile("D:\\github\\uffs-arquivos\\SEM4\\org\\processador8bits\\inst_decoder.vhd")) u_INST_DECODER (
    .operation(u_INSTRUCTION_MEMORY_instruction), .reg_dest(out_2), .reg_a(out_3), .reg_b(out_4),
    .inst_code(out_5), .cnst(out_10));
  // Probe on u_INST_MEM_CONTROLLER_instruction_addrs
  RAMDualPort #(.AddrBits(5), .Bits(12)) ramdualport_1 (
    .A(u_INST_MEM_CONTROLLER_instruction_addrs), .Din(u_INST_MEM_CONTROLLER_din),
    .str(u_INST_MEM_CONTROLLER_str), .C(in_26), .ld(u_INST_MEM_CONTROLLER_id), .D(ramdualport_1_d));
  INST_DECODER #(.applicationType("GHDL"), .CodeFile("D:\\github\\uffs-arquivos\\SEM4\\org\\processador8bits\\inst_decoder.vhd")) u_INST_DECODER_2 (
    .operation(ramdualport_1_d), .reg_dest(out_28), .reg_a(out_29), .reg_b(out_30), .inst_code(out_31),
    .cnst(out_32));
  RAMDualPort #(.AddrBits(5), .isProgramMemory("true"), .Bits(12)) ramdualport_2 (
    .A(\endereço_onde_pegar___armazenar ), .Din(dado_a_ser_armazenado_2),
    .str(_1___dado_armazenado_no_clock), .C(in_23), .ld(in_24), .D(out_19));
endmodule
